# Fritzing sketch Misol_WindSensor (saved by Fritzing 0.9.9b)
breadboards: 1

parts:
  S1 = SWITCH-MOMENTARY-2 [package=reed_switch_pth]
  S3 = SWITCH-MOMENTARY-2 [package=reed_switch_pth]
  R1 = Resistor [tolerance=±1% resistance=33k power=0.25 package=THT]
  S4 = SWITCH-MOMENTARY-2 [package=reed_switch_pth]
  S5 = SWITCH-MOMENTARY-2 [package=reed_switch_pth]
  S6 = SWITCH-MOMENTARY-2 [package=reed_switch_pth]
  S7 = SWITCH-MOMENTARY-2 [package=reed_switch_pth]
  S8 = SWITCH-MOMENTARY-2 [package=reed_switch_pth]
  S2 = SWITCH-MOMENTARY-2 [package=reed_switch_pth]
  R2 = Resistor [tolerance=±1% resistance=8.2k power=0.25 package=THT]
  R3 = Resistor [tolerance=±1% resistance=1k power=0.25 package=THT]
  R4 = Resistor [tolerance=±1% resistance=2.2k power=0.25 package=THT]
  R5 = Resistor [tolerance=±1% resistance=3.9k power=0.25 package=THT]
  R6 = Resistor [tolerance=±1% resistance=16k power=0.25 package=THT]
  R7 = Resistor [tolerance=±1% resistance=120k power=0.25 package=THT]
  R8 = Resistor [tolerance=±1% resistance=64.9k power=0.25 package=THT]
  Swind = SWITCH-MOMENTARY-2 [package=reed_switch_pth]
  RJ11 = RJ11 Jack [package=rj11-6]

nets:
  N1: S1.1, R1.Pin_0
  N2: S1.2, S3.2, S4.2, S5.2, S6.2, S7.2, S8.2, S2.2, RJ11.2
  N3: S3.1, R3.Pin_0
  N4: R1.Pin_1, R2.Pin_1, R3.Pin_1, R4.Pin_1, R5.Pin_1, R6.Pin_1, R7.Pin_1, R8.Pin_1, Swind.1, RJ11.4, RJ11.5
  N5: S4.1, R4.Pin_0
  N6: S5.1, R5.Pin_0
  N7: S6.1, R6.Pin_0
  N8: S7.1, R7.Pin_0
  N9: S8.1, R8.Pin_0
  N10: S2.1, R2.Pin_0
  N11: Swind.2, RJ11.3

notes:
  ref WH-SP-WD
  ref WH-SP-WS
  black
  red
  green
  yellow

custom parts:
  RJ11 Jack: RJ11 Jack6 pin RJ11 jack stright
