# Fritzing sketch WindSensor (saved by Fritzing 0.9.4)
breadboards: 2

parts:
  ABX00014 = Arduino MKR Fox 1200
  S1 = SWITCH-MOMENTARY-2 [package=reed_switch_pth]
  S3 = SWITCH-MOMENTARY-2 [package=reed_switch_pth]
  R1 = Resistor [tolerance=±1% resistance=33k package=THT]
  S4 = SWITCH-MOMENTARY-2 [package=reed_switch_pth]
  S5 = SWITCH-MOMENTARY-2 [package=reed_switch_pth]
  S6 = SWITCH-MOMENTARY-2 [package=reed_switch_pth]
  S7 = SWITCH-MOMENTARY-2 [package=reed_switch_pth]
  S8 = SWITCH-MOMENTARY-2 [package=reed_switch_pth]
  S2 = SWITCH-MOMENTARY-2 [package=reed_switch_pth]
  R2 = Resistor [tolerance=±1% resistance=8.2k package=THT]
  R3 = Resistor [tolerance=±1% resistance=1k package=THT]
  R4 = Resistor [tolerance=±1% resistance=2.2k package=THT]
  R5 = Resistor [tolerance=±1% resistance=3.9k package=THT]
  R6 = Resistor [tolerance=±1% resistance=16k package=THT]
  R7 = Resistor [tolerance=±1% resistance=120k package=THT]
  R8 = Resistor [tolerance=±1% resistance=64.9k package=THT]
  R9 = Resistor [tolerance=±1% resistance=10k package=THT]
  S9 = SWITCH-MOMENTARY-2 [package=reed_switch_pth]
  RJ11 = RJ11 Jack [package=rj11-6]
  U1 = TVS [package=sma-diode]
  U2 = TVS [package=sma-diode]
  MT3068_+_TP4056 = Power Cell LiPo Charger/Booster
  18650_holder = 18650 holder [package="DIP (Dual Inline) [THT]"]
  18650_holder2 = 18650 holder [package="DIP (Dual Inline) [THT]"]
  18650_holder3 = 18650 holder [package="DIP (Dual Inline) [THT]"]
  PV_5V_1A = Solar Panel [package="Renogy 50 Watts 12 Volt Monocrystalline Bendable Solar Panel"]
  R10 = Resistor [tolerance=±1% resistance=560k package=THT]
  R11 = Resistor [tolerance=±1% resistance=390k package=THT]
  C2 = Film/Foil Capacitor [capacitance=100nF voltage=35V package="7.5mm [THT, pp]"]

nets:
  N1: ABX00014.A4, R10.Pin_0, R11.Pin_1, C2.+
  pinGirAdc: ABX00014.A6, S1.2, S3.2, S4.2, S5.2, S6.2, S7.2, S8.2, S2.2, R9.Pin_0, RJ11.4, U1.1
  intPinAnemo: ABX00014.~4, S9.2, RJ11.5, U2.1
  pinGirAlim: ABX00014.~5, R9.Pin_1
  GND: ABX00014.GND, R1.Pin_1, R2.Pin_1, R3.Pin_1, R4.Pin_1, R5.Pin_1, R6.Pin_1, R7.Pin_1, R8.Pin_1, S9.1, RJ11.2, RJ11.3, U1.2, U2.2, MT3068_+_TP4056.GND, 18650_holder.holder_-, PV_5V_1A.Connector_2, R11.Pin_0, C2.-
  VIN: ABX00014.VIN, MT3068_+_TP4056.VCC
  N2: S1.1, R1.Pin_0
  N3: S3.1, R3.Pin_0
  N4: S4.1, R4.Pin_0
  N5: S5.1, R5.Pin_0
  N6: S6.1, R6.Pin_0
  N7: S7.1, R7.Pin_0
  N8: S8.1, R8.Pin_0
  N9: S2.1, R2.Pin_0
  N10: MT3068_+_TP4056.5VIN, PV_5V_1A.Connector_1
  Vbat: MT3068_+_TP4056.VBATT, 18650_holder.holder_+, R10.Pin_1
  N11: 18650_holder.battery_+, 18650_holder2.holder_+
  N12: 18650_holder.battery_-, 18650_holder2.holder_-
  N13: 18650_holder2.battery_+, 18650_holder3.holder_+
  N14: 18650_holder2.battery_-, 18650_holder3.holder_-

notes:
  ref WH-SP-WD
  ref WH-SP-WS

custom parts:
  18650 holder: Акум формата 18650 в холдере
  Solar Panel: Renogy 50 Watts 12 Volt Solar Panel
